// Logisim project LookAheadCarry.circ as structural Verilog: 1 circuit, main circuit main
module main (
  input  [3:0] Y,
  input  [3:0] X,
  input  C0,
  input  X1
);

  wire and_1_out, and_2_out, and_3_out, and_4_out, and_5_out, and_6_out, C1_out, C2_out, C3_out, G0_out,
       G1_out, G2_out, G3_out, P0_out, P0C0_out, P0P1C0_out, P1_out, P1G0_out, P2_out, P2G1_out, P3_out;
  wire [0:0] C4_out;
  wire [3:0] S0_out;

  xor P2 (P2_out, X[2], Y[2]);
  xor P1 (P1_out, X[1], Y[1]);
  and G1 (G1_out, X[1], Y[1]);
  and G2 (G2_out, X[2], Y[2]);
  xor P3 (P3_out, C0, Y[3]);
  and G0 (G0_out, X[0], Y[0]);
  xor P0 (P0_out, X[0], Y[0]);
  xor S0 (S0_out[0], P0_out, C0);
  and P0C0 (P0C0_out, P0_out, C0);
  xor S1 (S0_out[1], P1_out, C1_out);
  and P1G0 (P1G0_out, P1_out, G0_out);
  and P0P1C0 (P0P1C0_out, P1_out, P0_out, C0);
  xor xor_1 (S0_out[2], P2_out, C2_out);
  and P2G1 (P2G1_out, P2_out, G1_out);
  and and_1 (and_1_out, P2_out, P1_out, G0_out);
  and and_2 (and_2_out, P2_out, P1_out, P0_out, G0_out);
  xor xor_2 (S0_out[3], P3_out, C3_out);
  and and_3 (and_3_out, P3_out, G2_out);
  and and_4 (and_4_out, P3_out, P2_out, G1_out);
  and and_5 (and_5_out, P3_out, P2_out, P1_out, G0_out);
  and and_6 (and_6_out, P3_out, P2_out, P1_out, P0_out, C0);
  and G3 (G3_out, C0, Y[3]);
  or C1 (C1_out, P0C0_out, G0_out);
  or C2 (C2_out, P1G0_out, P0P1C0_out, G1_out);
  or C3 (C3_out, P2G1_out, and_1_out, and_2_out, G2_out);
  or C4 (C4_out[0], and_3_out, and_4_out, and_5_out, and_6_out, G3_out);
  Hex_Digit_Display hex_digit_display_1 (.value(S0_out));  // open: dp
  Hex_Digit_Display hex_digit_display_2 (.value({{3{C0}}, C4_out[0]}));  // open: dp

  assign X[3] = C0;
  assign X1 = X[1];
endmodule
