// Logisim project Register.circ as structural Verilog: 1 circuit, main circuit main
module main (
  input  I3,
  input  I2,
  input  I1,
  input  I0,
  input  Left_Shift,
  input  Right_Shift,
  input  [1:0] in_7,
  input  Set,
  input  Reset
);

  wire Clk_out, d_ff_1_q, d_ff_2_q, d_ff_3_q, d_ff_4_q, multiplexer_1_out, multiplexer_2_out,
       multiplexer_3_out, multiplexer_4_out;

  Clock Clk (.out(Clk_out));
  Multiplexer #(.select(2)) multiplexer_1 (
    .in0(d_ff_1_q), .in1(Left_Shift), .in2(d_ff_2_q), .in3(I3), .out(multiplexer_1_out), .sel(in_7));
  D_Flip_Flop d_ff_1 (.D(multiplexer_1_out), .clk(Clk_out), .Q(d_ff_1_q), .preset(Set), .reset(Reset));  // open: Qn
  Multiplexer #(.select(2)) multiplexer_2 (
    .in0(d_ff_2_q), .in1(d_ff_1_q), .in2(d_ff_3_q), .in3(I2), .out(multiplexer_2_out), .sel(in_7));
  D_Flip_Flop d_ff_2 (.D(multiplexer_2_out), .clk(Clk_out), .Q(d_ff_2_q), .preset(Set), .reset(Reset));  // open: Qn
  Multiplexer #(.select(2)) multiplexer_3 (
    .in0(d_ff_3_q), .in1(d_ff_2_q), .in2(d_ff_4_q), .in3(I1), .out(multiplexer_3_out), .sel(in_7));
  D_Flip_Flop d_ff_3 (.D(multiplexer_3_out), .clk(Clk_out), .Q(d_ff_3_q), .preset(Set), .reset(Reset));  // open: Qn
  Multiplexer #(.select(2)) multiplexer_4 (
    .in0(d_ff_4_q), .in1(d_ff_3_q), .in2(Right_Shift), .in3(I0), .out(multiplexer_4_out), .sel(in_7));
  D_Flip_Flop d_ff_4 (.D(multiplexer_4_out), .clk(Clk_out), .Q(d_ff_4_q), .preset(Set), .reset(Reset));  // open: Qn
  LED led_1 (.in(d_ff_4_q));
  LED led_2 (.in(d_ff_3_q));
  LED led_3 (.in(d_ff_2_q));
  LED led_4 (.in(d_ff_1_q));
endmodule
